// Logisim project Projeto_Arquitetura-CC3MB.circ as structural Verilog: 8 circuits, main circuit main
module main (
  input  [3:0] A,
  input  [3:0] B,
  input  [2:0] Operacoes,
  output out_4,
  output out_5,
  output [3:0] S
);

  wire decoder_1_s0, decoder_1_s1, decoder_1_s2, decoder_1_s4;
  wire [3:0] add_4_1_out_5, sub_4_1_out_5;

  Decoder decoder_1 (
    .in_1(Operacoes), .S0(decoder_1_s0), .S1(decoder_1_s1), .S2(decoder_1_s2), .S4(decoder_1_s4));  // open: S3, S5, S6, S7
  Buffer buffer_1 (.B(B), .in_2(decoder_1_s0), .S(S));
  ADD_4 add_4_1 (.in_1(A), .in_2(B), .out_4(out_4), .in_3(1'b0), .out_5(add_4_1_out_5));
  Buffer buffer_2 (.B(add_4_1_out_5), .in_2(decoder_1_s1), .S(S));
  SUB_4 sub_4_1 (.in_1(A), .out_4(out_5), .in_2(B), .in_3(1'b0), .out_5(sub_4_1_out_5));
  Buffer buffer_3 (.B(sub_4_1_out_5), .in_2(decoder_1_s2), .S(S));
  inversor_controlado inversor_controlado_1 (.B(B), .in_2(decoder_1_s4), .S(S));
endmodule

module ADD_1 (
  input  A,
  input  B,
  input  Vem_C,
  output Soma,
  output Vai
);

  wire A_B_C_2_out, A_B_out, B_C_2_out, B_C_out;

  xor A_B (A_B_out, A, B);
  xor A_B_C (Soma, A_B_out, Vem_C);
  or B_C (B_C_out, B, Vem_C);
  and B_C_2 (B_C_2_out, B, Vem_C);
  and A_B_C_2 (A_B_C_2_out, B_C_out, A);
  or or_1 (Vai, A_B_C_2_out, B_C_2_out);
endmodule

module ADD_4 (
  input  [3:0] in_1,
  input  [3:0] in_2,
  input  in_3,
  output out_4,
  output [3:0] out_5
);

  wire add_1_2_vai, add_1_3_vai, add_1_4_vai;

  ADD_1 add_1_1 (.A(in_1[3]), .B(in_2[3]), .Vem_C(add_1_2_vai), .Soma(out_5[3]), .Vai(out_4));
  ADD_1 add_1_2 (.A(in_1[2]), .B(in_2[2]), .Vem_C(add_1_4_vai), .Soma(out_5[2]), .Vai(add_1_2_vai));
  ADD_1 add_1_3 (.A(in_1[0]), .B(in_2[0]), .Vem_C(in_3), .Soma(out_5[0]), .Vai(add_1_3_vai));
  ADD_1 add_1_4 (.A(in_1[1]), .B(in_2[1]), .Vem_C(add_1_3_vai), .Soma(out_5[1]), .Vai(add_1_4_vai));
endmodule

module SUB_1 (
  input  A,
  input  B,
  input  Vem_C,
  output Subtrai,
  output Vai
);

  wire A_B_C_2_out, A_B_out, B_C_2_out, B_C_out, not_1_out;

  xor A_B (A_B_out, A, B);
  not not_1 (not_1_out, A);
  xor A_B_C (Subtrai, A_B_out, Vem_C);
  or B_C (B_C_out, B, Vem_C);
  and B_C_2 (B_C_2_out, B, Vem_C);
  and A_B_C_2 (A_B_C_2_out, B_C_out, not_1_out);
  or or_1 (Vai, A_B_C_2_out, B_C_2_out);
endmodule

module SUB_4 (
  input  [3:0] in_1,
  input  [3:0] in_2,
  input  in_3,
  output out_4,
  output [3:0] out_5
);

  wire sub_1_2_vai, sub_1_3_vai, sub_1_4_vai;

  SUB_1 sub_1_1 (.A(in_1[3]), .B(in_2[3]), .Vem_C(sub_1_2_vai), .Subtrai(out_5[3]), .Vai(out_4));
  SUB_1 sub_1_2 (.A(in_1[2]), .B(in_2[2]), .Vem_C(sub_1_3_vai), .Subtrai(out_5[2]), .Vai(sub_1_2_vai));
  SUB_1 sub_1_3 (.A(in_1[1]), .B(in_2[1]), .Vem_C(sub_1_4_vai), .Subtrai(out_5[1]), .Vai(sub_1_3_vai));
  SUB_1 sub_1_4 (.A(in_1[0]), .B(in_2[0]), .Vem_C(in_3), .Subtrai(out_5[0]), .Vai(sub_1_4_vai));
endmodule

module Buffer (
  input  [3:0] B,
  input  in_2,
  output [3:0] S
);

  assign S[3] = in_2 ? B[3] : 1'bz;  // Controlled_Buffer controlled_buffer_1
  assign S[2] = in_2 ? B[2] : 1'bz;  // Controlled_Buffer controlled_buffer_2
  assign S[1] = in_2 ? B[1] : 1'bz;  // Controlled_Buffer controlled_buffer_3
  assign S[0] = in_2 ? B[0] : 1'bz;  // Controlled_Buffer controlled_buffer_4
endmodule

module inversor_controlado (
  input  [3:0] B,
  input  in_2,
  output [3:0] S
);

  assign S[3] = in_2 ? ~B[3] : 1'bz;  // Controlled_Inverter controlled_inverter_1
  assign S[2] = in_2 ? ~B[2] : 1'bz;  // Controlled_Inverter controlled_inverter_2
  assign S[1] = in_2 ? ~B[1] : 1'bz;  // Controlled_Inverter controlled_inverter_3
  assign S[0] = in_2 ? ~B[0] : 1'bz;  // Controlled_Inverter controlled_inverter_4
endmodule

module Decoder (
  input  [2:0] in_1,
  output S0,
  output S1,
  output S2,
  output S3,
  output S4,
  output S5,
  output S6,
  output S7
);

  wire not_1_out, not_2_out, not_3_out, not_4_out, not_5_out, not_6_out, not_7_out, not_8_out, not_9_out,
       not_10_out, not_11_out, not_12_out;

  not not_1 (not_1_out, in_1[2]);
  not not_2 (not_2_out, in_1[1]);
  not not_3 (not_3_out, in_1[0]);
  not not_4 (not_4_out, in_1[2]);
  not not_5 (not_5_out, in_1[1]);
  not not_6 (not_6_out, in_1[2]);
  not not_7 (not_7_out, in_1[0]);
  not not_8 (not_8_out, in_1[2]);
  not not_9 (not_9_out, in_1[1]);
  not not_10 (not_10_out, in_1[0]);
  not not_11 (not_11_out, in_1[1]);
  not not_12 (not_12_out, in_1[0]);
  and and_1 (S7, in_1[2], in_1[1], in_1[0]);
  and and_2 (S0, not_1_out, not_2_out, not_3_out);
  and and_3 (S1, not_4_out, not_5_out, in_1[0]);
  and and_4 (S2, not_6_out, in_1[1], not_7_out);
  and and_5 (S3, not_8_out, in_1[1], in_1[0]);
  and and_6 (S4, in_1[2], not_9_out, not_10_out);
  and and_7 (S5, in_1[2], not_11_out, in_1[0]);
  and and_8 (S6, in_1[2], in_1[1], not_12_out);
endmodule
